# Fritzing sketch mk61avr_I2C (saved by Fritzing 0.9.0b)
circuit board: 13.9492cm x 15.1414cm
breadboards: 1
perfboards: 1

parts:
  R1 = Resistor [tolerance=±5% resistance=220 package=THT]
  9 = Momentary Switch [package=ksa_sealed_tac_switch]
  SS = Momentary Switch [package=ksa_sealed_tac_switch]
  Sub = Momentary Switch [package=ksa_sealed_tac_switch]
  Store = Momentary Switch [package=ksa_sealed_tac_switch]
  Goto = Momentary Switch [package=ksa_sealed_tac_switch]
  U1 = LCD-16X2 [package=lcd-16x2]
  D3 = Diode [package=diode-1n4001]
  POW = Momentary Switch [package=ksa_sealed_tac_switch]
  <- = Momentary Switch [package=ksa_sealed_tac_switch]
  x = Momentary Switch [package=ksa_sealed_tac_switch]
  Load = Momentary Switch [package=ksa_sealed_tac_switch]
  VCC1 = Battery
  F = Momentary Switch [package=ksa_sealed_tac_switch]
  XY = Momentary Switch [package=ksa_sealed_tac_switch]
  Cx = Momentary Switch [package=ksa_sealed_tac_switch]
  7 = Momentary Switch [package=ksa_sealed_tac_switch]
  / = Momentary Switch [package=ksa_sealed_tac_switch]
  Step-> = Momentary Switch [package=ksa_sealed_tac_switch]
  D7 = Diode [package=diode-1n4001]
  Load_2 = Momentary Switch [package=ksa_sealed_tac_switch]
  8 = Momentary Switch [package=ksa_sealed_tac_switch]
  - = Momentary Switch [package=ksa_sealed_tac_switch]
  0 = Momentary Switch [package=ksa_sealed_tac_switch]
  6 = Momentary Switch [package=ksa_sealed_tac_switch]
  D1 = Diode [package=diode-1n4001]
  Ret = Momentary Switch [package=ksa_sealed_tac_switch]
  R4 = Resistor [tolerance=±5% resistance=220 package=THT]
  -> = Momentary Switch [package=ksa_sealed_tac_switch]
  3 = Momentary Switch [package=ksa_sealed_tac_switch]
  2 = Momentary Switch [package=ksa_sealed_tac_switch]
  D10 = Diode [package=diode-1n4001]
  D6 = Diode [package=diode-1n4001]
  1 = Momentary Switch [package=ksa_sealed_tac_switch]
  D8 = Diode [package=diode-1n4001]
  D4 = Diode [package=diode-1n4001]
  IC1 = MICROCONTROLLER [package=dil28-3]
  D2 = Diode [package=diode-1n4001]
  4 = Momentary Switch [package=ksa_sealed_tac_switch]
  D5 = Diode [package=diode-1n4001]
  /-/ = Momentary Switch [package=ksa_sealed_tac_switch]
  D9 = Diode [package=diode-1n4001]
  + = Momentary Switch [package=ksa_sealed_tac_switch]
  Save = Momentary Switch [package=ksa_sealed_tac_switch]
  K = Momentary Switch [package=ksa_sealed_tac_switch]
  Bx = Momentary Switch [package=ksa_sealed_tac_switch]
  R2 = Resistor [tolerance=±5% resistance=220 package=THT]
  R3 = Resistor [tolerance=±5% resistance=220 package=THT]
  S2 = Momentary Switch [package=ksa_sealed_tac_switch]
  part = Momentary Switch [package=ksa_sealed_tac_switch]
  Step<- = Momentary Switch [package=ksa_sealed_tac_switch]
  5 = Momentary Switch [package=ksa_sealed_tac_switch]
  JP1 = Header 5x2 [package=2x5-shrouded_smd]
  LCM1602_IIC1 = LCM1602 IIC [part_number="LCM1602 IIC" chip_label="LCM1602 IIC" package="DIP (Dual Inline) [THT]"]
  X1 = DB9 Connector [package=db9]
  On/Off = Momentary Switch [package=ksa_sealed_tac_switch]

nets (from the breadboard view):
  N1: R1.Pin_0, <-.3, Load.3, ->.3, Save.3, On/Off.3
  N2: R1.Pin_1, IC1.PD5(T1)
  N3: 9.1, D1.A
  N4: 9.2, Bx.1
  N5: 9.3, 7.3, 8.3, 0.3, 6.3, 3.3, 2.3, 1.3, 4.3, R2.Pin_0, 5.3
  N6: SS.1, SS.3, Sub.1, Sub.2, Sub.3, Sub.4, Store.3, Goto.1, Goto.2, Goto.3, Goto.4, POW.2, POW.4, x.2, x.4, F.1, F.2, F.3, F.4, XY.4, Cx.4, /.2, /.4, Step->.1, Step->.2, Step->.3, Step->.4, Load_2.1, Load_2.3, -.2, -.4, Ret.1, Ret.3, R4.Pin_0, /-/.2, /-/.4, +.2, +.4, K.3, Bx.2, Bx.4, part.2, part.4, Step<-.1, Step<-.2, Step<-.3, Step<-.4
  N7: Store.1, XY.2
  VSS: U1.VSS, LCM1602_IIC1.VSS
  VDD: U1.VDD, LCM1602_IIC1.VDD
  N8: U1.VO, LCM1602_IIC1.V0
  N9: U1.RS, LCM1602_IIC1.RS
  N10: U1.R_W, LCM1602_IIC1.RW
  N11: U1.E, LCM1602_IIC1.E
  N12: U1.DB0, LCM1602_IIC1.D0
  N13: U1.DB1, LCM1602_IIC1.D1
  N14: U1.DB2, LCM1602_IIC1.D2
  N15: U1.DB3, LCM1602_IIC1.D3
  N16: U1.DB4, LCM1602_IIC1.D4
  N17: U1.DB5, LCM1602_IIC1.D5
  N18: U1.DB6, LCM1602_IIC1.D6
  N19: U1.DB7, LCM1602_IIC1.D7
  N20: U1.A, LCM1602_IIC1.A
  N21: U1.K, LCM1602_IIC1.K
  N22: D3.A, <-.1
  N23: D3.C, IC1.PB1(OC1A)
  N24: POW.1, 7.2
  N25: POW.3, x.3, XY.3, Cx.3, /.3, -.3, /-/.3, +.3, Bx.3, R3.Pin_0, part.3
  N26: <-.2, 1.1
  N27: x.1, 2.2
  N28: Load.1, D6.A
  N29: Load.2, 4.1
  GND: VCC1.-, IC1.GND, IC1.AGND, S2.3, S2.4, LCM1602_IIC1.GND, X1.5
  VCC: VCC1.+, IC1.VCC, IC1.AVCC, LCM1602_IIC1.VCC
  N30: XY.1, 4.2
  N31: Cx.1, 8.2
  N32: Cx.2, K.1
  N33: 7.1, D9.A
  N34: /.1, 3.2
  N35: D7.A, 5.1
  N36: D7.C, IC1.PB5(SCK), JP1.7
  N37: 8.1, D10.A
  N38: -.1, 1.2
  N39: 0.1, On/Off.2
  N40: 0.2, +.1
  N41: 6.1, D8.A
  N42: 6.2, /-/.1
  N43: D1.C, IC1.PC1(ADC1)
  N44: R4.Pin_1, IC1.PD2(INT0)
  N45: ->.1, D4.A
  N46: ->.2, 2.1
  N47: 3.1, Save.2
  N48: D10.C, IC1.PC0(ADC0)
  N49: D6.C, IC1.PB4(MISO), JP1.9
  N50: D8.C, IC1.PB6(XTAL1_TOSC1)
  N51: D4.C, IC1.PB2(SS_OC1B)
  N52: IC1.PC6(_RESET), S2.1, S2.2, JP1.5
  N53: IC1.PD0(RXD), X1.8
  N54: IC1.PD1(TXD), X1.7
  N55: IC1.PD3(INT1), R3.Pin_1
  N56: IC1.PD4(XCK_T0), R2.Pin_1
  N57: IC1.PB7(XTAL2_TOSC2), D9.C
  N58: IC1.PB0(ICP), D2.C
  N59: IC1.PB3(MOSI_OC2), D5.C, JP1.1, JP1.3
  N60: D2.A, On/Off.1
  N61: D5.A, Save.1
  N62: part.1, 5.2
  N63: JP1.4, JP1.6, JP1.8, JP1.10
  N64: LCM1602_IIC1.LED_A, LCM1602_IIC1.LED_B

notes:
  Столбцы клавиатуры - PB0-7 и PC0-1 (10 шт)
  Строки клавиатуры - PD2-5 (4шт)

custom parts:
  LCM1602 IIC: I2C-Module to use a 1602 or 2004 LCD on with the wire.h libory Serial LCD Modul
